// Logisim project vj1.circ as structural Verilog: 8 circuits, main circuit main
module main (
  input  a,
  input  b,
  input  s,
  output o
);

  wire and_1_out, and_2_out;

  and and_1 (and_1_out, a, s);
  and and_2 (and_2_out, b, ~s);  // AND_Gate
  or or_1 (o, and_1_out, and_2_out);
endmodule

module mux2to1 (
  input  a,
  input  b,
  input  s,
  output o
);

  wire and_1_out, and_2_out, not_1_out;

  not not_1 (not_1_out, s);
  and and_1 (and_1_out, a, s);
  and and_2 (and_2_out, b, not_1_out);
  or or_1 (o, and_1_out, and_2_out);
endmodule

module mux4to1 (
  input  a,
  input  b,
  input  c,
  input  d,
  input  [1:0] in_5,
  output o
);

  wire mux2to1_1_o, mux2to1_2_o;

  mux2to1 mux2to1_1 (.o(mux2to1_1_o), .s(in_5[0]), .b(b), .a(a));
  mux2to1 mux2to1_2 (.o(mux2to1_2_o), .s(in_5[0]), .b(d), .a(c));
  mux2to1 mux2to1_3 (.o(o), .s(in_5[1]), .b(mux2to1_2_o), .a(mux2to1_1_o));
endmodule

module SRLatch (
  input  r,
  input  s,
  output q,
  output qn
);

  nor nor_1 (q, r, qn);
  nor nor_2 (qn, q, s);
endmodule

module DLatch (
  input  c,
  input  d,
  output q
);

  wire and_1_out, and_2_out;

  and and_1 (and_1_out, c, ~d);  // AND_Gate
  and and_2 (and_2_out, c, d);
  SRLatch srlatch_1 (.r(and_1_out), .s(and_2_out), .q(q));  // open: qn
endmodule

module DFlipFlop (
  input  c,
  input  d,
  output q
);

  wire dlatch_1_q, not_1_out;

  not not_1 (not_1_out, c);
  DLatch dlatch_1 (.c(c), .d(d), .q(dlatch_1_q));
  DLatch dlatch_2 (.c(not_1_out), .d(dlatch_1_q), .q(q));
endmodule

module Reg4b (
  input  c,
  input  WriteEn,
  input  [3:0] data,
  output [3:0] out_4
);

  wire and_1_out;

  and and_1 (and_1_out, c, WriteEn);
  DFlipFlop dflipflop_1 (.c(and_1_out), .d(data[3]), .q(out_4[3]));
  DFlipFlop dflipflop_2 (.c(and_1_out), .d(data[2]), .q(out_4[2]));
  DFlipFlop dflipflop_3 (.c(and_1_out), .d(data[1]), .q(out_4[1]));
  DFlipFlop dflipflop_4 (.c(and_1_out), .d(data[0]), .q(out_4[0]));
endmodule

module RegFile (
  input  [3:0] in_1,
  input  [1:0] RA,
  input  C,
  input  WriteEn,
  input  [3:0] in_5,
  input  [3:0] in_6,
  input  [1:0] RB,
  input  [1:0] RW,
  input  [3:0] BusW
);

  wire and_1_out, and_2_out, and_3_out, decoder_1_out0, decoder_1_out1, decoder_1_out2, decoder_1_out3,
       decoder_2_out0, decoder_2_out1, decoder_2_out2, decoder_2_out3;
  wire [3:0] controlled_buffer_1_out, Reg1_out_4, Reg2_out_4, Reg3_out_4;

  Decoder #(.select(2)) decoder_1 (
    .out0(decoder_1_out0), .out1(decoder_1_out1), .out2(decoder_1_out2), .out3(decoder_1_out3), .sel(RA),
    .en(1'b1));
  Decoder #(.select(2)) decoder_2 (
    .out0(decoder_2_out0), .out1(decoder_2_out1), .out2(decoder_2_out2), .out3(decoder_2_out3), .sel(RW),
    .en(1'b1));
  and and_1 (and_1_out, decoder_2_out1, WriteEn);
  Reg4b Reg0 (.c(C), .data(BusW));  // open: WriteEn, out_4
  Reg4b Reg2 (.c(C), .WriteEn(and_1_out), .data(BusW), .out_4(Reg2_out_4));
  assign controlled_buffer_1_out = decoder_1_out3 ? Reg2_out_4 : 4'bz;  // Controlled_Buffer controlled_buffer_1
  Controlled_Buffer #(.width(4)) controlled_buffer_2 (.in(Reg2_out_4), .out(controlled_buffer_1_out));  // open: en
  and and_2 (and_2_out, decoder_2_out2, WriteEn);
  and and_3 (and_3_out, decoder_2_out3, WriteEn);
  Reg4b Reg1 (.c(C), .WriteEn(and_2_out), .data(BusW), .out_4(Reg1_out_4));
  Reg4b Reg3 (.c(C), .WriteEn(and_3_out), .data(BusW), .out_4(Reg3_out_4));
  assign controlled_buffer_1_out = decoder_1_out0 ? in_1 : 4'bz;  // Controlled_Buffer controlled_buffer_3
  assign controlled_buffer_1_out = decoder_1_out1 ? Reg1_out_4 : 4'bz;  // Controlled_Buffer controlled_buffer_4
  assign controlled_buffer_1_out = decoder_1_out2 ? Reg3_out_4 : 4'bz;  // Controlled_Buffer controlled_buffer_5
  Controlled_Buffer #(.width(4)) controlled_buffer_6 (.in(Reg3_out_4), .out(controlled_buffer_1_out));  // open: en
  Controlled_Buffer #(.width(4)) controlled_buffer_7 (.in(Reg1_out_4), .out(controlled_buffer_1_out));  // open: en
  // also tied to GND on the sheet: decoder_2_out0
endmodule
